# Fritzing sketch Coche_L298N_v8 (saved by Fritzing 0.9.10b)

parts:
  Motor_DI = DC Motor [voltage_(max)=6V voltage_(min)=3V]
  INA219 = INA219 DC Current Monitor Module [part_number=GY-219]
  S1 = Taiway 100-SP-X-T1 SPDT Miniature Toggle Switch [part_number=100-SP-X-T1-0-0-B1-M2 package=THT]
  ESP32_Dev_Kit_C_V4 = MH-ET LIVE ESP32 DEVKIT 38 pins
  U3 = LIPO-1000mAh [package=lipo-1000]
  U4 = LIPO-1000mAh [package=lipo-1000]
  L298N = L298N DC motor driver

nets:
  N1: Motor_DI.pin_1, L298N.OUT2
  N2: Motor_DI.pin_2, L298N.OUT1
  N3: INA219.Vin+, S1.L2
  N4: S1.COM, U4.+
  N5: ESP32_Dev_Kit_C_V4.IO32, L298N.IN2
  N6: ESP32_Dev_Kit_C_V4.IO33, L298N.IN1
  N7: ESP32_Dev_Kit_C_V4.IO25, L298N.ENA
  5V: ESP32_Dev_Kit_C_V4.5V, L298N.5V
  N8: U3.+, U4.-

custom parts:
  INA219 DC Current Monitor Module: INA219 DC Current Monitor Module Links: INA219 product information
  MH-ET LIVE ESP32 DEVKIT 38 pins: http://mh.nodebb.com/topic/2/mh-et-live-esp32-devkit
  L298N DC motor driver: 2x DC motor driver with 78M05 positive voltage regulator (7..35 V) L298N: max 46 V, 2 A Set 5 V Enable jumper to enable 5 V regultor (needed for the L298N) and +5 V output at screw terminal or supply external +5 V at screw terminal Set ENA and/or ENB to +5 V to enable motor permanently or supply ENA and/or ENB with PWM signal IN1 and IN2 set rotation directory for motor A (OUT1/OUT2) IN2 and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
