# Fritzing sketch Coche_v8 (saved by Fritzing 0.9.10b)

parts:
  L298N = L298N DC motor driver
  Motor_DD = DC Motor [voltage_(max)=6V voltage_(min)=3V]
  Motor_DI = DC Motor [voltage_(max)=6V voltage_(min)=3V]
  Motor_TD = DC Motor [voltage_(max)=6V voltage_(min)=3V]
  L298N_2 = L298N DC motor driver
  INA219 = INA219 DC Current Monitor Module [part_number=GY-219]
  S1 = Taiway 100-SP-X-T1 SPDT Miniature Toggle Switch [part_number=100-SP-X-T1-0-0-B1-M2 package=THT]
  Motor_TI = DC Motor [voltage_(max)=6V voltage_(min)=3V]
  ESP32_Dev_Kit_C_V4 = MH-ET LIVE ESP32 DEVKIT 38 pins
  Parado = LED - 5mm [color="Red (660nm)" current=0.030 package="5 mm [THT]"]
  Conectado = LED - 5mm [color="Green (570nm)" current=0.030 package="5 mm [THT]"]
  R2 = Resistor [tolerance=±5% power=0.25 resistance=220 package=THT]
  U3 = LIPO-1000mAh [package=lipo-1000]
  U4 = LIPO-1000mAh [package=lipo-1000]
  R1 = Resistor [tolerance=±5% power=0.25 resistance=220 package=THT]

nets:
  N1: L298N.OUT1, Motor_DI.pin_2
  N2: L298N.OUT2, Motor_DI.pin_1
  N3: L298N.OUT3, Motor_DD.pin_2
  N4: L298N.OUT4, Motor_DD.pin_1
  12V: L298N.12V, L298N_2.12V
  GND: L298N.GND, L298N_2.GND, INA219.GND, ESP32_Dev_Kit_C_V4.GND#58, U3.-
  5V: L298N.5V, ESP32_Dev_Kit_C_V4.5V
  N5: L298N.ENA, ESP32_Dev_Kit_C_V4.IO25
  N6: L298N.ENB, ESP32_Dev_Kit_C_V4.IO19
  N7: L298N.IN1, ESP32_Dev_Kit_C_V4.IO33
  N8: L298N.IN2, ESP32_Dev_Kit_C_V4.IO32
  N9: L298N.IN3, ESP32_Dev_Kit_C_V4.IO5
  N10: L298N.IN4, ESP32_Dev_Kit_C_V4.IO18
  N11: Motor_TD.pin_1, L298N_2.OUT4
  N12: Motor_TD.pin_2, L298N_2.OUT3
  N13: L298N_2.OUT1, Motor_TI.pin_2
  N14: L298N_2.OUT2, Motor_TI.pin_1
  N15: L298N_2.ENA, ESP32_Dev_Kit_C_V4.IO14
  N16: L298N_2.ENB, ESP32_Dev_Kit_C_V4.IO4
  N17: L298N_2.IN1, ESP32_Dev_Kit_C_V4.IO27
  N18: L298N_2.IN2, ESP32_Dev_Kit_C_V4.IO26
  N19: L298N_2.IN3, ESP32_Dev_Kit_C_V4.IO16
  N20: L298N_2.IN4, ESP32_Dev_Kit_C_V4.IO17
  VCC: INA219.VCC, ESP32_Dev_Kit_C_V4.3V3
  N21: INA219.SCL, ESP32_Dev_Kit_C_V4.TXD0
  N22: INA219.SDA, ESP32_Dev_Kit_C_V4.IO22
  N23: INA219.Vin+, S1.L2
  N24: S1.COM, U4.+
  N25: ESP32_Dev_Kit_C_V4.IO12, Parado.anode
  N26: ESP32_Dev_Kit_C_V4.IO13, Conectado.anode
  N27: ESP32_Dev_Kit_C_V4.GND#70, R2.Pin_0, R1.Pin_0
  N28: U3.+, U4.-

notes:
  Conectado
  Parado

custom parts:
  L298N DC motor driver: 2x DC motor driver with 78M05 positive voltage regulator (7..35 V) L298N: max 46 V, 2 A Set 5 V Enable jumper to enable 5 V regultor (needed for the L298N) and +5 V output at screw terminal or supply external +5 V at screw terminal Set ENA and/or ENB to +5 V to enable motor permanently or supply ENA and/or ENB with PWM signal IN1 and IN2 set rotation directory for motor A (OUT1/OUT2) IN2 and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
  INA219 DC Current Monitor Module: INA219 DC Current Monitor Module Links: INA219 product information
  MH-ET LIVE ESP32 DEVKIT 38 pins: http://mh.nodebb.com/topic/2/mh-et-live-esp32-devkit
